// Logisim project ProyectoMIPS.circ as structural Verilog: 6 circuits, main circuit main
// address
module main (
  input  Reset,
  input  Active_Store,
  input  Active_Load,
  input  Reset_2,
  input  [31:0] in_5,
  output [25:0] out_6,
  output [31:0] out_7,
  output [15:0] out_8,
  output [4:0] out_9,
  output [4:0] out_10,
  output [4:0] out_11,
  output [5:0] out_12
);

  wire clock;
  wire [23:0] pc_1_address;

  Clock clock_1 (.out(clock));
  PC pc_1 (.Reset(Reset), .Clock(clock), .Address(pc_1_address));
  RAM #(.addrWidth(24), .dataWidth(32), .bus("separate")) ram_1 (
    .addr(pc_1_address), .din(in_5), .data(out_7), .str(Active_Store), .clk(clock), .ld(Active_Load),
    .clr(Reset_2));  // open: sel
  Decode decode_1 (
    .in_1(out_7), .Address_J(out_6), .Address(out_8), .rs(out_9), .rt(out_10), .rd(out_11), .Funct_op(out_12));  // open: Shamt

  // Notes on the sheet:
  //   FETCH
endmodule

module PC (
  input  Clock,
  input  Reset,
  output [23:0] Address
);

  wire [23:0] adder_1_out;

  Adder #(.width(24)) adder_1 (.a(Address), .b(24'h1), .out(adder_1_out));  // open: cin, cout
  Register #(.width(24)) register_1 (.D(adder_1_out), .Q(Address), .clk(Clock), .clr(Reset));  // open: en
endmodule

module Decode (
  input  [31:0] in_1,
  output [25:0] Address_J,
  output [15:0] Address,
  output [4:0] rs,
  output [4:0] rt,
  output [4:0] rd,
  output [4:0] Shamt,
  output [5:0] Funct_op
);

  wire not_1_out;
  wire [1:0] comparator_2_eq;
  wire [25:0] demultiplexer_1_out0, demultiplexer_1_out1;

  Comparator #(.width(6)) comparator_1 (.a(in_1[31:26]), .b({6{1'b0}}), .eq(comparator_2_eq[1]));  // open: gt, lt
  Demultiplexer #(.width(26), .enable("false")) demultiplexer_1 (
    .out0(demultiplexer_1_out0), .out1({demultiplexer_1_out1[25:16], rd, Shamt, demultiplexer_1_out1[5:0]}),
    .in(in_1[25:0]), .sel(comparator_2_eq[1]));
  Comparator #(.width(6)) comparator_2 (.a(in_1[31:26]), .b(6'b000010), .eq(comparator_2_eq[0]));  // open: gt, lt
  Multiplexer #(.width(6), .enable("false")) multiplexer_1 (
    .in0(demultiplexer_1_out1[5:0]), .in1(in_1[31:26]), .out(Funct_op), .sel(not_1_out));
  not not_1 (not_1_out, comparator_2_eq[1]);
  Multiplexer #(.width(16), .enable("false")) multiplexer_2 (
    .in0(demultiplexer_1_out0[15:0]), .in1({16{1'b0}}), .out(Address), .sel(comparator_2_eq[0]));
  Multiplexer #(.width(26), .enable("false")) multiplexer_3 (
    .in0({26{1'b0}}), .in1(demultiplexer_1_out0), .out(Address_J), .sel(comparator_2_eq[0]));
  Multiplexer #(.select(2), .width(10), .enable("false")) multiplexer_4 (
    .in0(demultiplexer_1_out0[25:16]), .in1({10{1'b0}}), .in2(demultiplexer_1_out1[25:16]), .out({rs, rt}),
    .sel(comparator_2_eq));  // open: in3
endmodule

module Show_Will (
  input  [4:0] rs,
  input  [4:0] rt,
  input  [4:0] rd,
  input  [4:0] Shamt,
  input  [5:0] Funct_op,
  input  [15:0] address,
  input  [25:0] address_J
);

  wire num_1_out_2, num_1_out_3, num_1_out_4, num_1_out_5, num_1_out_6, num_1_out_7, num_1_out_8,
       num_2_out_2, num_2_out_3, num_2_out_4, num_2_out_5, num_2_out_6, num_2_out_7, num_2_out_8,
       num_3_out_2, num_3_out_3, num_3_out_4, num_3_out_5, num_3_out_6, num_3_out_7, num_3_out_8,
       num_4_out_2, num_4_out_3, num_4_out_4, num_4_out_5, num_4_out_6, num_4_out_7, num_4_out_8,
       num_5_out_2, num_5_out_3, num_5_out_4, num_5_out_5, num_5_out_6, num_5_out_7, num_5_out_8;

  _7_Segment_Display u_7_segment_display_1 (
    .g(num_1_out_5), .f(num_1_out_4), .a(num_1_out_3), .b(num_1_out_2), .e(num_1_out_8), .d(num_1_out_7),
    .c(num_1_out_6));  // open: dp
  num num_1 (
    .in_1(rs[0]), .out_8(num_1_out_8), .out_7(num_1_out_7), .out_6(num_1_out_6), .out_5(num_1_out_5),
    .out_4(num_1_out_4), .out_3(num_1_out_3), .out_2(num_1_out_2));
  _7_Segment_Display u_7_segment_display_2 (
    .g(num_2_out_5), .f(num_2_out_4), .a(num_2_out_3), .b(num_2_out_2), .e(num_2_out_8), .d(num_2_out_7),
    .c(num_2_out_6));  // open: dp
  num num_2 (
    .in_1(rs[1]), .out_8(num_2_out_8), .out_7(num_2_out_7), .out_6(num_2_out_6), .out_5(num_2_out_5),
    .out_4(num_2_out_4), .out_3(num_2_out_3), .out_2(num_2_out_2));
  _7_Segment_Display u_7_segment_display_3 (
    .g(num_3_out_5), .f(num_3_out_4), .a(num_3_out_3), .b(num_3_out_2), .e(num_3_out_8), .d(num_3_out_7),
    .c(num_3_out_6));  // open: dp
  num num_3 (
    .in_1(rs[2]), .out_8(num_3_out_8), .out_7(num_3_out_7), .out_6(num_3_out_6), .out_5(num_3_out_5),
    .out_4(num_3_out_4), .out_3(num_3_out_3), .out_2(num_3_out_2));
  _7_Segment_Display u_7_segment_display_4 (
    .g(num_4_out_5), .f(num_4_out_4), .a(num_4_out_3), .b(num_4_out_2), .e(num_4_out_8), .d(num_4_out_7),
    .c(num_4_out_6));  // open: dp
  num num_4 (
    .in_1(rs[3]), .out_8(num_4_out_8), .out_7(num_4_out_7), .out_6(num_4_out_6), .out_5(num_4_out_5),
    .out_4(num_4_out_4), .out_3(num_4_out_3), .out_2(num_4_out_2));
  _7_Segment_Display u_7_segment_display_5 (
    .g(num_5_out_5), .f(num_5_out_4), .a(num_5_out_3), .b(num_5_out_2), .e(num_5_out_8), .d(num_5_out_7),
    .c(num_5_out_6));  // open: dp
  num num_5 (
    .in_1(rs[4]), .out_8(num_5_out_8), .out_7(num_5_out_7), .out_6(num_5_out_6), .out_5(num_5_out_5),
    .out_4(num_5_out_4), .out_3(num_5_out_3), .out_2(num_5_out_2));
endmodule

module num (
  input  in_1,
  output out_2,
  output out_3,
  output out_4,
  output out_5,
  output out_6,
  output out_7,
  output out_8
);

  Multiplexer #(.width(7), .enable("false")) multiplexer_1 (
    .in0(7'b1110111), .in1(7'b0010001), .out({out_8, out_7, out_6, out_5, out_4, out_3, out_2}), .sel(in_1));
endmodule

module ShowOp_funct (
  input  [5:0] Funct_0p
);

  wire comparator_1_eq, comparator_2_eq, comparator_3_eq, comparator_4_eq, comparator_5_eq, comparator_6_eq,
       comparator_7_eq, comparator_8_eq, comparator_9_eq, comparator_10_eq;
  wire [6:0] multiplexer_3_out;

  Comparator #(.width(6)) comparator_1 (.a(Funct_0p), .b(6'b100000), .eq(comparator_1_eq));  // open: gt, lt
  Comparator #(.width(6)) comparator_2 (.a(Funct_0p), .b(6'b100010), .eq(comparator_2_eq));  // open: gt, lt
  Comparator #(.width(6)) comparator_3 (.a(Funct_0p), .b(6'b100100), .eq(comparator_3_eq));  // open: gt, lt
  Comparator #(.width(6)) comparator_4 (.a(Funct_0p), .b(6'b100000), .eq(comparator_4_eq));  // open: gt, lt
  Comparator #(.width(6)) comparator_5 (.a(Funct_0p), .b(6'b100000), .eq(comparator_5_eq));  // open: gt, lt
  Comparator #(.width(6)) comparator_6 (.a(Funct_0p), .b(6'b100000), .eq(comparator_6_eq));  // open: gt, lt
  Comparator #(.width(6)) comparator_7 (.a(Funct_0p), .b(6'b100000), .eq(comparator_7_eq));  // open: gt, lt
  Comparator #(.width(6)) comparator_8 (.a(Funct_0p), .b(6'b100000), .eq(comparator_8_eq));  // open: gt, lt
  Comparator #(.width(6)) comparator_9 (.a(Funct_0p), .b(6'b100000), .eq(comparator_9_eq));  // open: gt, lt
  Comparator #(.width(6)) comparator_10 (.a(Funct_0p), .b(6'b100000), .eq(comparator_10_eq));  // open: gt, lt
  Multiplexer #(.width(7), .enable("false")) multiplexer_1 (.in1(7'b1110111), .sel(comparator_1_eq));  // open: in0, out
  Multiplexer #(.width(7), .enable("false")) multiplexer_2 (.in1(7'b1110111), .sel(comparator_2_eq));  // open: in0, out
  Multiplexer #(.width(7), .enable("false")) multiplexer_3 (
    .in1(7'b1110111), .out(multiplexer_3_out), .sel(comparator_2_eq));  // open: in0
  Multiplexer #(.width(7), .enable("false")) multiplexer_4 (.in1(7'b1110111), .sel(comparator_2_eq));  // open: in0, out
endmodule
